# Fritzing sketch Stimmungslaterne (saved by Fritzing 0.9.3b)
breadboards: 1

parts:
  neopixel1 = Neopixel Ring 12
  Bauteil1 = Arduino Nano (Rev3.0)
  YwRobot_Power_Supply2 = YwRobot Breadboard Power Supply [part_number=545043]
  Part1 = KY-022 Infrared Receiver Module [package="Breakout board"]

nets:
  GND: neopixel1.GND, Bauteil1.GND, YwRobot_Power_Supply2.GND#11, YwRobot_Power_Supply2.GND#12, Part1.-
  VCC: neopixel1.VCC, Bauteil1.5V, YwRobot_Power_Supply2.VCC#5, YwRobot_Power_Supply2.VCC#6, Part1.Vin
  N1: neopixel1.IN, Bauteil1.D6
  N2: Bauteil1.D11/MOSI, Part1.S
  N3: YwRobot_Power_Supply2.VCC#9, YwRobot_Power_Supply2.VCC#10
  N4: YwRobot_Power_Supply2.GND#13, YwRobot_Power_Supply2.GND#14

custom parts:
  Neopixel Ring 12: Neopixel Ring x12
  YwRobot Breadboard Power Supply: The YwRobot Breadboard Power Supply (MB-V2) has two power rails; they can be 5V or 3V3. Power to the module can be provided through the female USB socket or through the A10 (female) 2.1mm power jack.
  KY-022 Infrared Receiver Module: Arduino IR receiver module KY-022, reacts to 38kHz infrared light.
